# Fritzing sketch Sonic Screwdriver v4.3 (saved by Fritzing 0.9.6b)
circuit board: 4.5cm x 2.2cm
breadboards: 1

parts:
  Motor = Vibration Motor- ROB-08449 [package=vibe-motor-10mm]
  J1 = female pin header, 9 pins [form="♀ (female)"]
  J2 = female pin header, 9 pins [form="♀ (female)"]
  Connector2 = female pin header, 8 pins [form="♀ (female)"]
  S = female pin header, 1 pin [form="♀ (female)"]
  GND = female pin header, 1 pin [form="♀ (female)"]
  Wifi_EN = Pushbutton [package="[THT]"]
  Battery = female pin header, 3 pins [form="♀ (female)"]
  Tsistor = NPN-Transistor [package="TO92 [THT]"]
  Connector1 = female pin header, 8 pins [form="♀ (female)"]

nets:
  N1: Motor.+, J2.pin6
  N2: Motor.-, J2.pin2, Connector2.pin1, Connector2.pin2, GND.pin1, Wifi_EN.Pin_1, Wifi_EN.Pin_2, Battery.pin2, Tsistor.E, Connector1.pin5, Connector1.pin6
  N3: J1.pin3, Tsistor.B
  N4: J1.pin4, Connector1.pin2
  N5: J1.pin5, J2.pin3, Connector2.pin3, Connector1.pin3, Connector1.pin4
  N6: J1.pin6, Connector2.pin6
  N7: J1.pin7, Connector2.pin7
  N8: J1.pin8, Connector2.pin8
  N9: J2.pin1, Battery.pin1, Battery.pin3, Connector1.pin8
  N10: J2.pin4, Wifi_EN.Pin_3, Wifi_EN.Pin_4
  N11: J2.pin5, Connector1.pin1
  N12: J2.pin7, Connector2.pin5
  N13: J2.pin8, Connector2.pin4
  N14: J2.pin9, S.pin1
  N15: Tsistor.C, Connector1.pin7

notes:
  GND   S1 S2
  R  G  B
  ~5V TXGND  GND     3v3   RX  LED
  This is Sonic Device v4.3 © James Glynn 2024
  This design is licensed under the GPL3.0 license
